// Digital circuit frontpanelCOPY.dig as structural Verilog
module frontpanelCOPY (
  input  [15:0] A,
  input  [15:0] B,
  input  [15:0] A_2,
  input  [15:0] B_2,
  input  [15:0] A_3,
  input  [15:0] B_3,
  input  [15:0] A_4,
  input  [15:0] B_4,
  output [15:0] Result,
  output [15:0] Result_2,
  output [15:0] Result_3,
  output [15:0] Result_4
);

  wire _32b_1x2_decoder_1_p3, button_1_out, demultiplexer_2_out_0, demultiplexer_2_out_1,
       demultiplexer_2_out_2, demultiplexer_2_out_3;
  wire [1:0] PC_out;
  wire [15:0] _32b_1x2_decoder_1_p2, demultiplexer_1_out_0, demultiplexer_1_out_1, demultiplexer_1_out_2,
       demultiplexer_1_out_3, execute_1_result, multiplexer_2_out, multiplexer_3_out, multiplexer_4_out,
       multiplexer_5_out;
  wire [31:0] multiplexer_1_out;

  Counter #(.Bits(2), .isProgramCounter("true")) PC (
    .en(1'b1), .C(button_1_out), .clr(1'b0), .out(PC_out));  // open: ovf
  Button button_1 (.out(button_1_out));
  Multiplexer #(.Bits(32), .Selector_Bits(2)) multiplexer_1 (
    .sel(PC_out), .in_0({B, A}), .in_1({B_2, A_2}), .in_2({B_3, A_3}), .in_3({B_4, A_4}),
    .out(multiplexer_1_out));
  // _32b_1x2_decoder _32b_1x2_decoder_1: pin names not known; wires that end beside it: multiplexer_1_out, _32b_1x2_decoder_1_p2, _32b_1x2_decoder_1_p3
  Execute execute_1 (.A(_32b_1x2_decoder_1_p2), .add(_32b_1x2_decoder_1_p3), .Result(execute_1_result));  // open: B
  Demultiplexer #(.Bits(16), .Selector_Bits(2)) demultiplexer_1 (
    .sel(PC_out), .in(execute_1_result), .out_0(demultiplexer_1_out_0), .out_1(demultiplexer_1_out_1),
    .out_2(demultiplexer_1_out_2), .out_3(demultiplexer_1_out_3));
  Demultiplexer #(.Selector_Bits(2)) demultiplexer_2 (
    .sel(PC_out), .in(1'b1), .out_0(demultiplexer_2_out_0), .out_1(demultiplexer_2_out_1),
    .out_2(demultiplexer_2_out_2), .out_3(demultiplexer_2_out_3));
  Multiplexer #(.Bits(16)) multiplexer_2 (
    .sel(demultiplexer_2_out_0), .in_0(Result), .in_1(demultiplexer_1_out_0), .out(multiplexer_2_out));
  Multiplexer #(.Bits(16)) multiplexer_3 (
    .sel(demultiplexer_2_out_1), .in_0(Result_3), .in_1(demultiplexer_1_out_1), .out(multiplexer_3_out));
  Multiplexer #(.Bits(16)) multiplexer_4 (
    .sel(demultiplexer_2_out_2), .in_0(Result_4), .in_1(demultiplexer_1_out_2), .out(multiplexer_4_out));
  Multiplexer #(.Bits(16)) multiplexer_5 (
    .sel(demultiplexer_2_out_3), .in_0(Result_2), .in_1(demultiplexer_1_out_3), .out(multiplexer_5_out));
  D_FF #(.Bits(16)) d_ff_1 (.D(multiplexer_2_out), .C(button_1_out), .Q(Result));  // open: nQ
  D_FF #(.Bits(16)) d_ff_2 (.D(multiplexer_3_out), .C(button_1_out), .Q(Result_3));  // open: nQ
  D_FF #(.Bits(16)) d_ff_3 (.D(multiplexer_4_out), .C(button_1_out), .Q(Result_4));  // open: nQ
  D_FF #(.Bits(16)) d_ff_4 (.D(multiplexer_5_out), .C(button_1_out), .Q(Result_2));  // open: nQ

  // Notes on the sheet:
  //   A: default 40
  //   B: default 30
  //   A_2: default 100
  //   B_2: default 85
  //   A_3: default 180
  //   B_3: default 65
  //   A_4: default 4
  //   B_4: default 5
endmodule
