// Digital circuit 32b_1x2_decoder.dig as structural Verilog
module _32b_1x2_decoder (
  input  mode,
  input  [31:0] bypass,
  input  [31:0] \input ,
  output [15:0] A,
  output [1:0] rs,
  output [1:0] rd
);

  wire [31:18] multiplexer_1_out;

  Multiplexer #(.Bits(32)) multiplexer_1 (
    .sel(mode), .in_0(\input ), .in_1(bypass),
    .out({multiplexer_1_out[31:22], rs, multiplexer_1_out[19:18], rd, A}));
endmodule
