// Digital circuit assembler.dig as structural Verilog
module assembler (
  input  mode,
  input  [15:0] imm,
  input  [1:0] dest,
  input  [1:0] src,
  input  ADD,
  input  JMP,
  output [31:0] inst,
  output clock
);

  wire instruction_any;

  PriorityEncoder #(.Selector_Bits(3)) instruction (
    .in0(ADD), .in1(1'b0), .in2(1'b0), .in3(1'b0), .in4(1'b0), .in5(1'b0), .in6(1'b0), .in7(JMP),
    .num(inst[26:24]), .any(instruction_any));
  and and_1 (clock, instruction_any, mode);

  assign {inst[31:27], inst[23:0]} = {{7{1'b0}}, src, 2'b00, dest, imm};
endmodule
