// Digital circuit frontpanel.dig as structural Verilog
module frontpanel (
  input  [1:0] src,
  input  [1:0] dest,
  input  [15:0] value,
  output [15:0] R0,
  output [15:0] R1,
  output [15:0] R2,
  output [15:0] R3,
  output [15:0] B,
  output [1:0] rd,
  output [15:0] A,
  output [15:0] B_2,
  output [1:0] rs
);

  wire ADD_out, assembler_1_clock, button_1_out, JMP_out, mode_out;
  wire [1:0] PC_out;
  wire [15:0] execute_1_p3;
  wire [31:0] assembler_1_inst, program_d;

  Button ADD (.out(ADD_out));
  Button JMP (.out(JMP_out));
  DipSwitch mode (.out(mode_out));
  LED led_1 (.in(mode_out));
  assembler assembler_1 (
    .mode(mode_out), .imm(value), .dest(dest), .src(src), .ADD(ADD_out), .JMP(JMP_out),
    .inst(assembler_1_inst), .clock(assembler_1_clock));
  Button button_1 (.out(button_1_out));
  Counter #(.Bits(2), .isProgramCounter("true")) PC (
    .en(1'b1), .C(button_1_out), .clr(1'b0), .out(PC_out));  // open: ovf
  EEPROMDualPort #(.Bits(32)) \program  (
    .A(PC_out), .Din(assembler_1_inst), .str(1'b1), .C(assembler_1_clock), .ld(1'b1), .D(program_d));
  _32b_1x2_decoder _32b_1x2_decoder_1 (
    .mode(mode_out), .bypass(assembler_1_inst), .\input (program_d), .A(A), .rs(rs), .rd(rd));
  // Execute execute_1: pin names not known; wires that end beside it: A, B, execute_1_p3, B, R0, R1, R2, R3
  register_file register_file_1 (
    .rs(rs), .rd(rd), .result(execute_1_p3), .clock(button_1_out), .B(B));  // open: R0, R1, R2, R3

  assign B_2 = B;

  // Notes on the sheet:
  //   contents of program (hex, n*v repeats v):
  //   10028,120064,230064,30000f
endmodule
