// Digital circuit 32b_1x2_decoder.dig as structural Verilog
module _32b_1x2_decoder (
  input  [31:0] \input ,
  output [1:0] rs,
  output [1:0] rd,
  output [15:0] V,
  output add,
  output jmp
);

  Decoder #(.Selector_Bits(3)) decoder_1 (
    .sel(\input [26:24]), .out_0(add), .out_7(jmp));  // open: out_1, out_2, out_3, out_4, out_5, out_6

  assign rd = \input [17:16];
  assign rs = \input [21:20];
  assign V = \input [15:0];
endmodule
