// Digital circuit Execute.dig as structural Verilog
module Execute (
  input  [15:0] A,
  input  [15:0] B,
  input  add,
  output [15:0] Result
);

  wire [15:0] Adder_s;

  Add #(.Bits(16)) Adder (.a(A), .b(B), .c_i(1'b0), .s(Adder_s));  // open: c_o
  Multiplexer #(.Bits(16)) multiplexer_1 (.sel(add), .in_0(B), .in_1(Adder_s), .out(Result));
endmodule
