// Digital circuit fetch.dig as structural Verilog
module fetch (
  input  mode,
  input  [31:0] byp_inst,
  input  [31:0] inst_i,
  input  adv_clk,
  input  [15:0] value,
  input  jmp,
  output [3:0] PC,
  output [31:0] inst
);

  CounterPreset #(.Bits(4)) counterpreset_1 (
    .en(1'b1), .C(adv_clk), .dir(1'b0), .in(value[3:0]), .ld(jmp), .clr(1'b0), .out(PC));  // open: ovf
  Multiplexer #(.Bits(32)) multiplexer_1 (.sel(mode), .in_0(inst_i), .in_1(byp_inst), .out(inst));
endmodule
