// Digital circuit frontpanel.dig as structural Verilog
module frontpanel (
  input  [1:0] src,
  input  [1:0] dest,
  input  [15:0] value,
  output [15:0] R0,
  output [15:0] R1,
  output [15:0] R2,
  output [15:0] R3,
  output [1:0] rd,
  output [15:0] A,
  output [15:0] B,
  output [1:0] rs,
  output [15:0] Addr
);

  wire add, ADD_out, adv_clock_out, assembler_1_store_clk, jmp, JMP_out, m_1_p1, m_1_p6, m_1_p7, m_1_p8,
       mode_out;
  wire [3:0] m_1_p4;
  wire [15:0] execute_1_result;
  wire [31:0] assembler_1_inst, fetch_1_p8, m_1_p5, program_d;

  Button u_ADD (.out(ADD_out));
  Button u_JMP (.out(JMP_out));
  Button adv_clock (.out(adv_clock_out));
  DipSwitch mode (.out(mode_out));
  LED led_1 (.in(mode_out));
  assembler assembler_1 (
    .mode(mode_out), .imm(value), .dest(dest), .src(src), .add(ADD_out), .jmp(JMP_out),
    .inst(assembler_1_inst), .store_clk(assembler_1_store_clk));
  // M m_1: pin names not known; wires that end beside it: m_1_p1, assembler_1_inst, assembler_1_store_clk, m_1_p4, m_1_p5, m_1_p6, m_1_p7, m_1_p8
  EEPROMDualPort #(.AddrBits(4), .Bits(32)) \program  (
    .A(m_1_p4), .Din(m_1_p5), .str(m_1_p6), .C(m_1_p7), .ld(m_1_p8), .D(program_d));
  LED JMP_2 (.in(jmp));
  LED ADD_2 (.in(add));
  // fetch fetch_1: pin names not known; wires that end beside it: mode_out, assembler_1_inst, program_d, adv_clock_out, A, jmp, m_1_p1, fetch_1_p8
  _32b_1x2_decoder _32b_1x2_decoder_1 (.\input (fetch_1_p8), .rs(rs), .rd(rd), .V(A), .add(add), .jmp(jmp));
  Execute execute_1 (.A(A), .B(B), .add(add), .Result(execute_1_result));
  // register_file register_file_1: pin names not known; wires that end beside it: rs, rd, execute_1_result, adv_clock_out, B, R0, R1, R2, R3

  assign Addr = A;

  // Other names for the same wires on the sheet: V[15:0] = A

  // Notes on the sheet:
  //   contents of program (hex, n*v repeats v):
  //   0,0,10064,30000f,7000000,4*0,6*10064,64
endmodule
