// Digital circuit 32b_1x2_decoderCOPY.dig as structural Verilog
module _32b_1x2_decoderCOPY (
  input  [31:0] Input,
  output [15:0] A,
  output [1:0] rs,
  output [1:0] rd
);

  // Pins of 1 and 16 bits meet at Input[15:0]

  assign A = Input[15:0];
  assign rd = Input[17:16];
  assign rs = Input[21:20];
endmodule
