// Digital circuit frontpanelCOPY.dig as structural Verilog
module frontpanelCOPY (
  input  [15:0] A,
  input  [3:0] SD,
  input  [15:0] A_2,
  input  [3:0] SD_2,
  input  [15:0] A_3,
  input  [3:0] SD_3,
  input  [15:0] A_4,
  input  [3:0] SD_4,
  output [15:0] R0,
  output [15:0] R1,
  output [15:0] R2,
  output [15:0] R3,
  output [15:0] B
);

  wire _32b_1x2_decoder_1_p2, button_1_out;
  wire [1:0] _32b_1x2_decoder_1_p3, _32b_1x2_decoder_1_p4, PC_out;
  wire [15:0] _32b_1x2_decoder_1_p5;
  wire [31:0] multiplexer_1_out;

  Counter #(.Bits(2), .isProgramCounter("true")) PC (
    .en(1'b1), .C(button_1_out), .clr(1'b0), .out(PC_out));  // open: ovf
  Button button_1 (.out(button_1_out));
  Multiplexer #(.Selector_Bits(2), .Bits(32)) multiplexer_1 (
    .sel(PC_out), .in_0({{12{1'b0}}, SD, A}), .in_1({{12{1'b0}}, SD_2, A_2}), .in_2({{12{1'b0}}, SD_3, A_3}),
    .in_3({{12{1'b0}}, SD_4, A_4}), .out(multiplexer_1_out));
  // _32b_1x2_decoder _32b_1x2_decoder_1: pin names not known; wires that end beside it: multiplexer_1_out, _32b_1x2_decoder_1_p2, _32b_1x2_decoder_1_p3, _32b_1x2_decoder_1_p4, _32b_1x2_decoder_1_p5, B, R0, R1, R2, R3
  Execute execute_1 (.add(_32b_1x2_decoder_1_p2), .R(B));  // open: L, Result
  register_file register_file_1 (
    .rs(_32b_1x2_decoder_1_p3), .rd(_32b_1x2_decoder_1_p4), .result(_32b_1x2_decoder_1_p5),
    .clock(button_1_out), .B(B));  // open: R0, R1, R2, R3

  // Notes on the sheet:
  //   A: default 40
  //   SD: default 30
  //   A_2: default 40
  //   SD_2: default 30
  //   A_3: default 40
  //   SD_3: default 30
  //   A_4: default 40
  //   SD_4: default 30
endmodule
