// Digital circuit 32b_1x2_decoderCOPY.dig as structural Verilog
module _32b_1x2_decoderCOPY (
  input  [31:0] Input,
  output [15:0] A,
  output [15:0] B
);

  // Pins of 1 and 16 bits meet at Input[15:0]
  // Pins of 1 and 16 bits meet at Input[31:16]

  assign A = Input[15:0];
  assign B = Input[31:16];
endmodule
