// Digital circuit frontpanelCOPY.dig as structural Verilog
module frontpanelCOPY (
  input  [15:0] A,
  input  [15:0] B,
  input  [15:0] A_2,
  input  [15:0] B_2,
  input  [15:0] A_3,
  input  [15:0] B_3,
  input  [15:0] A_4,
  input  [15:0] B_4,
  output [15:0] R0,
  output [15:0] R1,
  output [15:0] R2,
  output [15:0] R3,
  output [15:0] B_5
);

  wire _32b_1x2_decoder_1_p3, button_1_out;
  wire [1:0] PC_out;
  wire [15:0] _32b_1x2_decoder_1_p2, execute_1_result;
  wire [31:0] multiplexer_1_out;

  Counter #(.Bits(2), .isProgramCounter("true")) PC (
    .en(1'b1), .C(button_1_out), .clr(1'b0), .out(PC_out));  // open: ovf
  Button button_1 (.out(button_1_out));
  Multiplexer #(.Selector_Bits(2), .Bits(32)) multiplexer_1 (
    .sel(PC_out), .in_0({B, A}), .in_1({B_2, A_2}), .in_2({B_3, A_3}), .in_3({B_4, A_4}),
    .out(multiplexer_1_out));
  // _32b_1x2_decoder _32b_1x2_decoder_1: pin names not known; wires that end beside it: multiplexer_1_out, _32b_1x2_decoder_1_p2, _32b_1x2_decoder_1_p3
  Execute execute_1 (.A(_32b_1x2_decoder_1_p2), .add(_32b_1x2_decoder_1_p3), .Result(execute_1_result));  // open: B
  // register_file register_file_1: pin names not known; wires that end beside it: PC_out, PC_out, execute_1_result, button_1_out, B_5, R0, R1, R2, R3

  // Notes on the sheet:
  //   A: default 40
  //   B: default 30
  //   A_2: default 100
  //   B_2: default 85
  //   A_3: default 180
  //   B_3: default 65
  //   A_4: default 4
  //   B_4: default 5
endmodule
