// Digital circuit ExecuteCOPY.dig as structural Verilog
module ExecuteCOPY (
  input  [15:0] A,
  input  [15:0] B,
  output [15:0] Result
);

  Add #(.Bits(16)) Adder (.a(A), .b(B), .c_i(1'b0), .s(Result));  // open: c_o
endmodule
