// Digital circuit frontpanel.dig as structural Verilog
module frontpanel (
  input  [1:0] src,
  input  [1:0] dest,
  input  [15:0] value,
  input  _2reg,
  output [15:0] R0,
  output [15:0] R1,
  output [15:0] R2,
  output [15:0] R3,
  output [1:0] rd,
  output [15:0] L,
  output [15:0] R,
  output [1:0] rs,
  output [15:0] Addr
);

  wire add, ADD_out, adv_clock_out, assembler_1_store_clk, jmp, JMP_out, m_1_p1, m_1_p6, m_1_p7, m_1_p8,
       mode_out;
  wire [3:0] m_1_p4;
  wire [15:0] execute_1_result, register_file_1_rdval, register_file_1_rsval;
  wire [31:0] assembler_1_inst, fetch_1_p8, m_1_p5, program_d;

  Button u_ADD (.out(ADD_out));
  Button u_JMP (.out(JMP_out));
  Button adv_clock (.out(adv_clock_out));
  DipSwitch mode (.out(mode_out));
  LED led_1 (.in(mode_out));
  assembler assembler_1 (
    .mode(mode_out), .imm(value), .dest(dest), .src(src), ._2reg(_2reg), .add(ADD_out), .jmp(JMP_out),
    .inst(assembler_1_inst), .store_clk(assembler_1_store_clk));
  // M m_1: pin names not known; wires that end beside it: m_1_p1, assembler_1_inst, assembler_1_store_clk, m_1_p4, m_1_p5, m_1_p6, m_1_p7, m_1_p8
  EEPROMDualPort #(.AddrBits(4), .Bits(32)) \program  (
    .A(m_1_p4), .Din(m_1_p5), .str(m_1_p6), .C(m_1_p7), .ld(m_1_p8), .D(program_d));
  LED JMP_2 (.in(jmp));
  LED ADD_2 (.in(add));
  // fetch fetch_1: pin names not known; wires that end beside it: mode_out, assembler_1_inst, program_d, adv_clock_out, Addr, jmp, m_1_p1, fetch_1_p8
  _32b_1x2_decoder _32b_1x2_decoder_1 (
    .rdval(register_file_1_rdval), .rsval(register_file_1_rsval), .\input (fetch_1_p8), .rs(rs), .rd(rd),
    .add(add), .L(L), .R(Addr), .jmp(jmp));
  Execute execute_1 (.add(add), .L(L), .R(Addr), .Result(execute_1_result));
  register_file register_file_1 (
    .rs(rs), .rd(rd), .result(execute_1_result), .clock(adv_clock_out), .rdval(register_file_1_rdval),
    .rsval(register_file_1_rsval), .R0(R0), .R1(R1), .R2(R2), .R3(R3));

  assign R = Addr;

  // Notes on the sheet:
  //   contents of program (hex, n*v repeats v):
  //   0,0,10064,30000f,7000000,4*0,6*10064,64
endmodule
